# Fritzing sketch Peristaltic-Pump-Fritzing (saved by Fritzing 0.9.1b)
breadboards: 1

parts:
  Onderdeel1 = Arduino Uno (Rev3) - ICSP
  Stepper_Driver = mystery part, 16 pins [chip_label=DRV8825]
  I2C_LCD_interface = mystery part, 4 pins [chip_label="I2C Interface"]
  R1 = Rotary Potentiometer (Small) [maximum_resistance=100kΩ package=THT]
  S1 = Pushbutton [package=THT]
  C1 = Tantalum Capacitor [capacitance=0.1mF package="100 mil [THT, tantalum]"]
  M1 = Stepper Motor - Bipolar
  R2 = Resistor [tolerance=±5% resistance=10k package=THT]
  R3 = Resistor [tolerance=±5% resistance=10k package=THT]
  R4 = Resistor [tolerance=±5% resistance=10k package=THT]
  R5 = Resistor [tolerance=±5% resistance=10k package=THT]
  C2 = Tantalum Capacitor [capacitance=1μF package="100 mil [THT, tantalum]"]
  C3 = Tantalum Capacitor [capacitance=1μF package="100 mil [THT, tantalum]"]

nets:
  N1: Onderdeel1.A4/SDA, I2C_LCD_interface.pin3
  N2: Onderdeel1.A5/SCL, I2C_LCD_interface.pin4
  N3: Onderdeel1.5V, Stepper_Driver.pin2, Stepper_Driver.pin3, Stepper_Driver.pin4, Stepper_Driver.pin5, I2C_LCD_interface.pin2, R2.Pin_1, R3.Pin_0
  N4: Onderdeel1.GND, Stepper_Driver.pin9, Stepper_Driver.pin15, I2C_LCD_interface.pin1, R1.wiper, S1.leg1, C1.-, C2.-, C3.-
  N5: Onderdeel1.D2, R5.Pin_0, C3.+
  N6: Onderdeel1.D3_PWM, R4.Pin_1, C2.+
  N7: Onderdeel1.D4, Stepper_Driver.pin8
  N8: Onderdeel1.D5_PWM, Stepper_Driver.pin7
  N9: Onderdeel1.D6_PWM, Stepper_Driver.pin6
  N10: Onderdeel1.D7, S1.leg0
  N11: Onderdeel1.VIN, Stepper_Driver.pin16, C1.+
  N12: Stepper_Driver.pin11, M1.A
  N13: Stepper_Driver.pin12, M1.C
  N14: Stepper_Driver.pin13, M1.B
  N15: Stepper_Driver.pin14, M1.D
  N16: R1.leg1, R2.Pin_0, R4.Pin_0
  N17: R1.leg2, R3.Pin_1, R5.Pin_1

notes:
  12V
  12V power supply
  Stepper Motor
  Stepper Driver
  Capacitor
  Rotary encoder
  debounce
  circuit
  Switch
  I2C LCD Interface
